# Fritzing sketch BoardDesign (saved by Fritzing 0.8.7b)
breadboards: 1

parts:
  U1 = 74HC4052 [package=dil16]
  U2 = 74HC4052 [package=dil16]
  T1 = TMP36 Temperature Sensor [package="TO92 [THT]"]
  Netduino1 = Netduino
  Part1 = GainSpan WiFi Breakout
  Debugger1 = Debugger
  AC_Remote1 = AC Remote

nets (from the breadboard view):
  GND: U1.INH, U1.GND, U2.INH, U2.GND, T1.GND, Netduino1.GND, Part1.GND, AC_Remote1.Gnd
  N1: U1.B, Netduino1.D10_PWM3
  N2: U1.A, Netduino1.D11_MOSI
  N3: U1.X0, AC_Remote1.Pin_?3
  N4: U1.X, U2.X
  N5: U1.X1, AC_Remote1.Pin_?1
  N6: U1.X2, AC_Remote1.Pin_?2
  VCC: U1.VCC, U2.VCC, T1.+Vs, Netduino1.Aref, Netduino1.3V3, Part1.3.3V, AC_Remote1.Vcc
  N7: U2.B, Netduino1.D4_CS0
  N8: U2.A, Netduino1.D5_PWM0
  N9: U2.X3, AC_Remote1.Pin8
  N10: U2.X0, AC_Remote1.Pin5
  N11: U2.X1, AC_Remote1.Pin6
  N12: U2.X2, AC_Remote1.Pin7
  N13: T1.Vout, Netduino1.A3
  N14: Netduino1.D8_CTS1, Part1.RST
  N15: Netduino1.D3_TX1, Debugger1.RX
  N16: Netduino1.D2_RX1, Debugger1.TX
  N17: Netduino1.D1_TX0, Part1.RX0
  N18: Netduino1.D0_RX0, Part1.TX0

custom parts:
  AC Remote: My AC Remote Control
